# Fritzing sketch buttonSwitch (saved by Fritzing 0.9.3b)
breadboards: 1

parts:
  R1 = Resistor [tolerance=±5% resistance=10k package=THT]
  Part1 = Arduino Uno (Rev3)
  S1 = Pushbutton [package="[SMD]"]
  LED1 = LED - 5mm [color="Red (633nm)" package="5 mm [THT]"]
  R2 = Resistor [tolerance=±5% resistance=470 package="0805 [SMD]"]

nets:
  N1: R1.Pin_0, Part1.GND, LED1.cathode
  N2: R1.Pin_1, Part1.D7, S1.Pin_3, S1.Pin_4
  N3: Part1.D13/SCK, R2.Pin_0
  N4: Part1.5V, S1.Pin_1, S1.Pin_2
  N5: LED1.anode, R2.Pin_1
